# Fritzing sketch Ultrasonic Distance ICEStick (saved by Fritzing 1.0.0rc)
breadboards: 3

parts:
  Bauteil1 = Lattice iCEstick
  Bauteil2 = TXB0108 8-channel Bi-directional Logic Level Converter
  D1 = LED_BARGRAPH_10 [package=led_bargaph_10]
  HC-SR04_Sensor_1 = HC-SR04 Ultrasonic Distance Sensor
  R1 = Resistor [tolerance=±5% power=0.25W resistance=220 package=THT]
  R2 = Resistor [tolerance=±5% power=0.25W resistance=220 package=THT]
  R3 = Resistor [tolerance=±5% power=0.25W resistance=220 package=THT]
  R4 = Resistor [tolerance=±5% power=0.25W resistance=220 package=THT]
  R5 = Resistor [tolerance=±5% power=0.25W resistance=220 package=THT]
  R7 = Resistor [tolerance=±5% power=0.25W resistance=220 package=THT]
  JP1 = USB_MICROB_PLUG [package=micro-b-smt]

nets:
  GND: Bauteil1.GND, Bauteil2.GND, HC-SR04_Sensor_1.GND, R1.Pin_0, R2.Pin_0, R3.Pin_0, R4.Pin_0, R5.Pin_0, R7.Pin_0, JP1.GND
  N1: Bauteil1.3V3, Bauteil2.OE, Bauteil2.VCCA
  N2: Bauteil1.112, Bauteil2.A8
  N3: Bauteil1.113, Bauteil2.A7
  N4: Bauteil1.114, Bauteil2.A6
  N5: Bauteil1.115, Bauteil2.A5
  N6: Bauteil1.116, Bauteil2.A4
  N7: Bauteil1.117, Bauteil2.A3
  N8: Bauteil1.118, Bauteil2.A2
  N9: Bauteil1.119, Bauteil2.A1
  N10: Bauteil2.B1, D1.D_A
  N11: Bauteil2.B2, D1.E_A
  N12: Bauteil2.B3, D1.F_A
  N13: Bauteil2.B4, D1.G_A
  N14: Bauteil2.B5, D1.H_A
  N15: Bauteil2.B6, D1.I_A
  N16: Bauteil2.B7, HC-SR04_Sensor_1.TRIG
  N17: Bauteil2.B8, HC-SR04_Sensor_1.ECHO
  VCC: HC-SR04_Sensor_1.VCC, JP1.VCC

custom parts:
  TXB0108 8-channel Bi-directional Logic Level Converter: Because the Arduino (and Basic Stamp) are 5V devices, and most modern sensors, displays, flash cards and modes are 3.3V-only, many makers find that they need to perform level shifting/conversion to protect the 3.3V device from 5V. Although one can use resistors to make a divider, for high speed transfers, the resistors can add a lot of slew and cause havoc that is tough to debug. For that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
